// Logisim project cpu_hw4.circ as structural Verilog: 5 circuits, main circuit main
module main (
);

  wire alu_1_ble, and_1_out, and_2_out, clock_1_out, controllogic_1_aluctrlenabled, controllogic_1_alusrc,
       controllogic_1_branch, controllogic_1_call, controllogic_1_halt, controllogic_1_jump,
       controllogic_1_memread, controllogic_1_memtoreg, controllogic_1_memwrite, controllogic_1_reboot,
       controllogic_1_regdst, controllogic_1_regwrite, controllogic_1_rtn, not_1_out, not_2_out, not_3_out,
       or_1_out;
  wire [2:0] alucontrol_1_operation, controllogic_1_aluop, multiplexer_4_out;
  wire [15:0] adder_1_out, adder_2_out, alu_1_aluout, bit_extender_1_out, DataMemory_dout,
       InstructionMemory_data, multiplexer_1_out, multiplexer_2_out, multiplexer_3_out, multiplexer_5_out,
       multiplexer_6_out, PC_q, ra_q, registerfile_1_readdata1, registerfile_1_readdata2;

  Clock clock_1 (.out(clock_1_out));
  Register #(.width(16)) PC (.D(multiplexer_3_out), .en(not_1_out), .clk(clock_1_out), .Q(PC_q));  // open: clr
  not not_1 (not_1_out, controllogic_1_halt);
  Adder #(.width(16)) adder_1 (.a(16'h1), .b(PC_q), .out(adder_1_out));  // open: cin, cout
  Adder #(.width(16)) adder_2 (.a(PC_q), .b(bit_extender_1_out), .out(adder_2_out));  // open: cin, cout
  or or_1 (or_1_out, and_2_out, controllogic_1_jump, controllogic_1_call);
  not not_2 (not_2_out, controllogic_1_halt);
  ROM #(.addrWidth(16), .dataWidth(16)) InstructionMemory (.addr(PC_q), .data(InstructionMemory_data));
  Multiplexer #(.enable("false"), .width(16)) multiplexer_1 (
    .in0(adder_1_out), .in1(adder_2_out), .out(multiplexer_1_out), .sel(or_1_out));
  Register #(.width(16)) ra (.D(adder_1_out), .en(and_1_out), .clk(clock_1_out), .Q(ra_q));  // open: clr
  and and_1 (and_1_out, controllogic_1_call, not_2_out);
  Multiplexer #(.enable("false"), .width(16)) multiplexer_2 (
    .in0(multiplexer_1_out), .in1(ra_q), .out(multiplexer_2_out), .sel(controllogic_1_rtn));
  Multiplexer #(.enable("false"), .width(16)) multiplexer_3 (
    .in0(multiplexer_2_out), .in1({16{1'b0}}), .out(multiplexer_3_out), .sel(controllogic_1_reboot));
  assign bit_extender_1_out = {{10{InstructionMemory_data[5]}}, InstructionMemory_data[5:0]};  // Bit_Extender bit_extender_1
  ControlLogic controllogic_1 (
    .opcode(InstructionMemory_data[15:12]), .ALUOp(controllogic_1_aluop), .Jump(controllogic_1_jump),
    .halt(controllogic_1_halt), .MemRead(controllogic_1_memread), .Call(controllogic_1_call),
    .RegDst(controllogic_1_regdst), .MemWrite(controllogic_1_memwrite), .Rtn(controllogic_1_rtn),
    .ALUSrc(controllogic_1_alusrc), .Branch(controllogic_1_branch), .Reboot(controllogic_1_reboot),
    .MemtoReg(controllogic_1_memtoreg), .ALUCtrlEnabled(controllogic_1_aluctrlenabled),
    .RegWrite(controllogic_1_regwrite));
  Multiplexer #(.enable("false"), .width(3)) multiplexer_4 (
    .in0(InstructionMemory_data[8:6]), .in1(InstructionMemory_data[5:3]), .out(multiplexer_4_out),
    .sel(controllogic_1_regdst));
  RegisterFile registerfile_1 (
    .clock(clock_1_out), .halt(controllogic_1_halt), .writeEnabled(controllogic_1_regwrite),
    .writeReg(multiplexer_4_out), .writeData(multiplexer_6_out), .readReg1(InstructionMemory_data[11:9]),
    .readReg2(InstructionMemory_data[8:6]), .readData1(registerfile_1_readdata1),
    .readData2(registerfile_1_readdata2));
  Multiplexer #(.enable("false"), .width(16)) multiplexer_5 (
    .in0(registerfile_1_readdata2), .in1(bit_extender_1_out), .out(multiplexer_5_out),
    .sel(controllogic_1_alusrc));
  and and_2 (and_2_out, controllogic_1_branch, alu_1_ble);
  ALU alu_1 (
    .operand1(registerfile_1_readdata1), .operand2(multiplexer_5_out), .operation(alucontrol_1_operation),
    .ALUOut(alu_1_aluout), .ble(alu_1_ble));
  ALUControl alucontrol_1 (
    .ALUOp(controllogic_1_aluop), .funct(InstructionMemory_data[2:0]),
    .ALUCtrlEnabled(controllogic_1_aluctrlenabled), .operation(alucontrol_1_operation));
  RAM #(.addrWidth(16), .dataWidth(16)) DataMemory (
    .addr(registerfile_1_readdata1), .we(controllogic_1_memwrite), .oe(controllogic_1_memread),
    .clk(not_3_out), .din(registerfile_1_readdata2), .dout(DataMemory_dout));
  not not_3 (not_3_out, clock_1_out);
  Multiplexer #(.enable("false"), .width(16)) multiplexer_6 (
    .in0(alu_1_aluout), .in1(DataMemory_dout), .out(multiplexer_6_out), .sel(controllogic_1_memtoreg));

  // Notes on the sheet:
  //   contents of InstructionMemory (hex, n*v repeats v):
  //   d001 d042 d08a 48 c2bf 5458 7000
endmodule

module RegisterFile (
  input  clock,
  input  halt,
  input  writeEnabled,
  input  [2:0] writeReg,
  input  [15:0] writeData,
  input  [2:0] readReg1,
  input  [2:0] readReg2,
  output [15:0] readData1,
  output [15:0] readData2
);

  wire and_1_out, decoder_1_out0, decoder_1_out1, decoder_1_out2, decoder_1_out3, decoder_1_out4,
       decoder_1_out5, decoder_1_out6, decoder_1_out7, not_1_out;
  wire [15:0] r1_q, r2_q, r3_q, r4_q, r5_q, r6_q, r7_q, r8_q;

  not not_1 (not_1_out, halt);
  and and_1 (and_1_out, not_1_out, writeEnabled);
  Decoder #(.select(3)) decoder_1 (
    .out0(decoder_1_out0), .out1(decoder_1_out1), .out2(decoder_1_out2), .out3(decoder_1_out3),
    .out4(decoder_1_out4), .out5(decoder_1_out5), .out6(decoder_1_out6), .out7(decoder_1_out7),
    .sel(writeReg), .en(and_1_out));
  Register #(.width(16)) r1 (.D(writeData), .en(decoder_1_out0), .clk(clock), .Q(r1_q));  // open: clr
  Register #(.width(16)) r2 (.D(writeData), .en(decoder_1_out1), .clk(clock), .Q(r2_q));  // open: clr
  Register #(.width(16)) r3 (.D(writeData), .en(decoder_1_out2), .clk(clock), .Q(r3_q));  // open: clr
  Register #(.width(16)) r4 (.D(writeData), .en(decoder_1_out3), .clk(clock), .Q(r4_q));  // open: clr
  Register #(.width(16)) r5 (.D(writeData), .en(decoder_1_out4), .clk(clock), .Q(r5_q));  // open: clr
  Register #(.width(16)) r6 (.D(writeData), .en(decoder_1_out5), .clk(clock), .Q(r6_q));  // open: clr
  Register #(.width(16)) r7 (.D(writeData), .en(decoder_1_out6), .clk(clock), .Q(r7_q));  // open: clr
  Register #(.width(16)) r8 (.D(writeData), .en(decoder_1_out7), .clk(clock), .Q(r8_q));  // open: clr
  Multiplexer #(.enable("false"), .select(3), .width(16)) multiplexer_1 (
    .in0(r1_q), .in1(r2_q), .in2(r3_q), .in3(r4_q), .in4(r5_q), .in5(r6_q), .in6(r7_q), .in7(r8_q),
    .out(readData1), .sel(readReg1));
  Multiplexer #(.enable("false"), .select(3), .width(16)) multiplexer_2 (
    .in0(r1_q), .in1(r2_q), .in2(r3_q), .in3(r4_q), .in4(r5_q), .in5(r6_q), .in6(r7_q), .in7(r8_q),
    .out(readData2), .sel(readReg2));
endmodule

module ALU (
  input  [15:0] operand1,
  input  [15:0] operand2,
  input  [2:0] operation,
  output [15:0] ALUOut,
  output ble
);

  wire comparator_1_eq, comparator_1_lt, comparator_2_lt;
  wire [15:0] adder_1_out, and_1_out, bit_extender_1_out, negator_1_out, or_1_out, shifter_1_out,
       shifter_2_out;

  Comparator #(.width(16)) comparator_1 (
    .a(operand1), .b(operand2), .eq(comparator_1_eq), .lt(comparator_1_lt));  // open: gt
  Comparator #(.width(16)) comparator_2 (.a(operand1), .b(operand2), .lt(comparator_2_lt));  // open: gt, eq
  Shifter #(.width(16)) shifter_1 (.in(operand1), .\dist (operand2[3:0]), .out(shifter_1_out));
  Shifter #(.shift("lr"), .width(16)) shifter_2 (.in(operand1), .\dist (operand2[3:0]), .out(shifter_2_out));
  Adder #(.width(16)) adder_1 (.a(operand1), .b(operand2), .out(adder_1_out));  // open: cin, cout
  Negator #(.width(16)) negator_1 (.in(operand1), .out(negator_1_out));
  assign and_1_out = operand1 & operand2;  // AND_Gate and_1, 16 bits wide
  assign or_1_out = operand1 | operand2;  // OR_Gate or_1, 16 bits wide
  or or_2 (ble, comparator_1_eq, comparator_1_lt);
  assign bit_extender_1_out = {{15{1'b0}}, comparator_2_lt};  // Bit_Extender bit_extender_1
  Multiplexer #(.enable("false"), .select(3), .width(16)) multiplexer_1 (
    .in0(adder_1_out), .in1(negator_1_out), .in2(and_1_out), .in3(or_1_out), .in4(operand2),
    .in5(bit_extender_1_out), .in6(shifter_1_out), .in7(shifter_2_out), .out(ALUOut), .sel(operation));
endmodule

module ALUControl (
  input  [2:0] ALUOp,
  input  [2:0] funct,
  input  ALUCtrlEnabled,
  output [2:0] operation
);

  wire [2:0] multiplexer_1_out;

  Multiplexer #(.enable("false"), .width(3)) multiplexer_1 (
    .in0(3'b000), .in1(funct), .out(multiplexer_1_out), .sel(ALUCtrlEnabled));
  assign operation = ALUOp | multiplexer_1_out;  // OR_Gate or_1, 3 bits wide
endmodule

module ControlLogic (
  input  [3:0] opcode,
  output [2:0] ALUOp,
  output Jump,
  output halt,
  output MemRead,
  output Call,
  output RegDst,
  output MemWrite,
  output Rtn,
  output ALUSrc,
  output Branch,
  output Reboot,
  output MemtoReg,
  output ALUCtrlEnabled,
  output RegWrite
);

  wire and_2_out, and_3_out, and_5_out, and_6_out, and_7_out, and_8_out, and_16_out, and_17_out, and_18_out,
       and_19_out, not_1_out, not_3_out, not_4_out, not_5_out, not_6_out, not_7_out, not_8_out, not_9_out,
       not_10_out, not_11_out, not_12_out, not_13_out, not_14_out, not_15_out, not_16_out, not_17_out,
       not_18_out, not_19_out, not_20_out, not_21_out, not_22_out, not_23_out, not_24_out, not_25_out,
       not_26_out, not_27_out, not_28_out, not_29_out, not_30_out, not_31_out, or_3_out, or_4_out;
  wire [2:0] multiplexer_1_out;

  not not_1 (not_1_out, opcode[3]);
  and and_1 (halt, not_1_out, opcode[2], opcode[1], opcode[0]);
  not not_2 (RegDst, opcode[3]);
  not not_3 (not_3_out, opcode[2]);
  and and_2 (and_2_out, opcode[3], not_3_out);
  or or_1 (ALUSrc, and_2_out, and_3_out);
  not not_4 (not_4_out, opcode[1]);
  and and_3 (and_3_out, opcode[3], not_4_out, opcode[0]);
  and and_4 (MemtoReg, opcode[3], opcode[2], opcode[1], not_5_out);
  not not_5 (not_5_out, opcode[0]);
  not not_6 (not_6_out, opcode[1]);
  not not_7 (not_7_out, opcode[3]);
  not not_8 (not_8_out, opcode[0]);
  and and_5 (and_5_out, not_6_out, not_7_out, not_8_out);
  or or_2 (RegWrite, and_5_out, and_6_out, and_7_out, and_8_out);
  not not_9 (not_9_out, opcode[1]);
  not not_10 (not_10_out, opcode[2]);
  and and_6 (and_6_out, opcode[2], opcode[0], not_9_out);
  and and_7 (and_7_out, opcode[3], not_10_out);
  not not_11 (not_11_out, opcode[0]);
  and and_8 (and_8_out, opcode[3], opcode[1], not_11_out);
  and and_9 (MemRead, opcode[3], opcode[2], opcode[1], not_12_out);
  not not_12 (not_12_out, opcode[0]);
  and and_10 (MemWrite, opcode[3], opcode[2], opcode[1], opcode[0]);
  not not_13 (not_13_out, opcode[1]);
  not not_14 (not_14_out, opcode[0]);
  and and_11 (Branch, opcode[3], opcode[2], not_13_out, not_14_out);
  nor nor_1 (ALUCtrlEnabled, opcode[3], opcode[2], opcode[1], opcode[0]);
  not not_15 (not_15_out, opcode[3]);
  not not_16 (not_16_out, opcode[2]);
  not not_17 (not_17_out, opcode[1]);
  not not_18 (not_18_out, opcode[3]);
  and and_12 (Jump, not_15_out, not_16_out, not_17_out, opcode[0]);
  not not_19 (not_19_out, opcode[3]);
  not not_20 (not_20_out, opcode[2]);
  not not_21 (not_21_out, opcode[2]);
  not not_22 (not_22_out, opcode[0]);
  and and_13 (Rtn, not_19_out, not_20_out, opcode[1], opcode[0]);
  and and_14 (Call, not_18_out, not_21_out, opcode[1], not_22_out);
  not not_23 (not_23_out, opcode[3]);
  not not_24 (not_24_out, opcode[0]);
  and and_15 (Reboot, not_23_out, opcode[2], opcode[1], not_24_out);
  not not_25 (not_25_out, opcode[1]);
  and and_16 (and_16_out, opcode[3], opcode[2], not_25_out, opcode[0]);
  not not_26 (not_26_out, opcode[3]);
  not not_27 (not_27_out, opcode[1]);
  not not_28 (not_28_out, opcode[0]);
  and and_17 (and_17_out, not_26_out, opcode[2], not_27_out, not_28_out);
  or or_3 (or_3_out, and_16_out, and_17_out);
  not not_29 (not_29_out, opcode[3]);
  not not_30 (not_30_out, opcode[1]);
  and and_18 (and_18_out, not_29_out, opcode[2], not_30_out, opcode[0]);
  not not_31 (not_31_out, opcode[2]);
  and and_19 (and_19_out, opcode[3], not_31_out);
  or or_4 (or_4_out, and_19_out, and_18_out);
  Multiplexer #(.enable("false"), .width(3)) multiplexer_1 (
    .in0(3'b000), .in1(opcode[2:0]), .out(multiplexer_1_out), .sel(or_4_out));
  Multiplexer #(.enable("false"), .width(3)) multiplexer_2 (
    .in0(multiplexer_1_out), .in1(3'b100), .out(ALUOp), .sel(or_3_out));
endmodule
